# Fritzing sketch lapcounter (saved by Fritzing 0.9.10b)
circuit board: 6.19984cm x 4.62941cm

parts:
  Part1 = Arduino Nano (Rev3.0)
  Buzz = Active Buzzer
  R1 = Trimmer Potentiometer [maximum_resistance=1kΩ knob_status=50% power=0.5W package=THT]
  J2 = MH-ET e-ink [package=THT]
  R2 = Trimmer Potentiometer [maximum_resistance=100kΩ knob_status=50% power=0.5W package=THT]
  R3 = Resistor [tolerance=±5% power=0.25 resistance=330k package=THT]
  LED1 = LED - 5mm [color="Red (633nm)" current=10mA package="5 mm [THT]"]
  CHECK = female pin header, 1 pin [form="♀ (female)"]
  C1 = Ceramic Capacitor [capacitance=100pF voltage=35V package="100 mil [THT, multilayer]"]
  MODES = DIP SWITCH [package=dipswitch-02]
  GND = female pin header, 1 pin [form="♀ (female)"]
  CAP = female pin header, 1 pin [form="♀ (female)"]
  R6 = Resistor [tolerance=±5% power=0.25 resistance=1k package=THT]
  R4 = Resistor [tolerance=±5% power=0.25 resistance=100k package=THT]
  R34 = Trimmer Potentiometer [maximum_resistance=1kΩ knob_status=50% power=0.5W package=THT]
  J3 = female pin header, 1 pin [form="♀ (female)"]
  J4 = female pin header, 10 pins [form="♀ (female)"]  # not connected
  R35 = Resistor [tolerance=±5% resistance=1k power=0.25 package="1206 [SMD]"]
  C3 = Ceramic Capacitor [capacitance=200pF voltage=35V package="100 mil [THT, multilayer]"]
  R36 = Resistor [tolerance=±5% power=0.25 resistance=20M package=THT]
  C2 = Electrolytic Capacitor [part_number=10uF voltage=35V capacitance=10μF package="200 mil [THT, electrolytic]"]

nets:
  GND: Part1.GND, Buzz.-, J2.GND, R2.leg1, C1.0, MODES.1, MODES.2, GND.pin1, R34.leg2, C3.1, C2.-
  N1: Part1.D4, R35.Pin_1
  N2: Part1.D5, R3.Pin_0
  N3: Part1.D7, J2.Busy
  N4: Part1.D8, J2.Reset
  N5: Part1.D9, J2.DC
  N6: Part1.D10, J2.CS
  N7: Part1.D11/MOSI, J2.SDI
  5V: Part1.5V, R1.wiper, J2.VCC, R2.leg2, C3.0, C2.+
  N8: Part1.A4, R2.wiper
  N9: Part1.A3, R4.Pin_0
  N10: Part1.A2, R6.Pin_0
  N11: Part1.A1, MODES.4
  N12: Part1.A0, MODES.3
  N13: Part1.D13/SCK, J2.SCLK, J3.pin1
  N14: Buzz.VCC, R1.leg1
  N15: Buzz.Signal, R35.Pin_0
  N16: R3.Pin_1, LED1.anode
  N17: LED1.cathode, R34.wiper
  N18: CHECK.pin1, R4.Pin_1, R36.Pin_1
  N19: C1.1, CAP.pin1, R6.Pin_1, R36.Pin_0

custom parts:
  Active Buzzer: Active Buzzer, GND, Signal, VCC.
  Electrolytic Capacitor: electrolytic capacitor
