# Fritzing sketch pot (saved by Fritzing 0.9.10b)
breadboards: 1

parts:
  R1 = Resistor [tolerance=±5% power=0.25 resistance=22M package=THT]
  R9 = Resistor [tolerance=±5% power=0.25 resistance=22M package=THT]
  R10 = Resistor [tolerance=±5% power=0.25 resistance=22M package=THT]
  R11 = Resistor [tolerance=±5% power=0.25 resistance=22M package=THT]
  R12 = Resistor [tolerance=±5% power=0.25 resistance=22M package=THT]
  R13 = Resistor [tolerance=±5% power=0.25 resistance=22M package=THT]
  R14 = Resistor [tolerance=±5% power=0.25 resistance=22M package=THT]
  R15 = Resistor [tolerance=±5% power=0.25 resistance=22M package=THT]
  R16 = Trimmer Potentiometer [maximum_resistance=1MΩ knob_status=50% power=0.5W package=THT]
  SW2 = DIP SWITCH [package=dipswitch-02]
  R17 = Resistor [tolerance=±5% power=0.25 resistance=100k package=THT]
  J1 = female pin header, 2 pins [form="♀ (female)"]
  SW3 = DIP SWITCH [package=dipswitch-02]
  OM1 = Multimeter (Ohmmeter)

nets:
  N1: R1.Pin_0, R9.Pin_0, R10.Pin_0, R11.Pin_0, SW2.4, J1.pin1, OM1.V_Probe
  N2: R1.Pin_1, R9.Pin_1, R10.Pin_1, R11.Pin_1, R12.Pin_0, R13.Pin_0, SW2.1, SW2.2
  N3: R12.Pin_1, R13.Pin_1, R15.Pin_0, SW2.3, SW3.4
  N4: R14.Pin_0, R15.Pin_1, SW3.1, SW3.2
  N5: R14.Pin_1, R16.wiper, SW3.3
  N6: R16.leg1, R17.Pin_1
  N7: R17.Pin_0, J1.pin2, OM1.COM_Probe
